# Fritzing sketch shematic (saved by Fritzing 0.9.3b)
breadboards: 1

parts:
  Part2 = Arduino Uno (Rev3)
  LED1 = LED - 5mm [color="Red (633nm)" package="5 mm [THT]"]  # not connected
  LED2 = LED - 5mm [color="Red (633nm)" package="5 mm [THT]"]  # not connected
  LED3 = LED - 5mm [color="Red (633nm)" package="5 mm [THT]"]  # not connected
  LED4 = LED - 5mm [color="Red (633nm)" package="5 mm [THT]"]  # not connected
  LED5 = LED - 5mm [color="Red (633nm)" package="5 mm [THT]"]  # not connected
  LED6 = LED - 5mm [color="Red (633nm)" package="5 mm [THT]"]  # not connected
  LED7 = LED - 5mm [color="Red (633nm)" package="5 mm [THT]"]  # not connected
  LED8 = LED - 5mm [color="Red (633nm)" package="5 mm [THT]"]  # not connected
  IC1 = IC, DIP package, 16 pins [chip_label=SN74HC595N]
  R1 = Resistor [tolerance=±5% resistance=330 package=THT]
  R2 = Resistor [tolerance=±5% resistance=330 package=THT]
  R3 = Resistor [tolerance=±5% resistance=330 package=THT]
  R4 = Resistor [tolerance=±5% resistance=330 package=THT]
  R5 = Resistor [tolerance=±5% resistance=330 package=THT]
  R6 = Resistor [tolerance=±5% resistance=330 package=THT]
  R8 = Resistor [tolerance=±5% resistance=330 package=THT]
  R9 = Resistor [tolerance=±5% resistance=330 package=THT]

nets:
  N1: Part2.GND, IC1.pin8, IC1.pin13, R1.Pin_0, R2.Pin_0, R3.Pin_0, R4.Pin_0, R5.Pin_0, R6.Pin_0, R8.Pin_0, R9.Pin_0
  N2: Part2.D2, IC1.pin14
  N3: Part2.D3_PWM, IC1.pin11
  N4: Part2.D4, IC1.pin12
  N5: Part2.5V, IC1.pin10, IC1.pin16
