# Fritzing sketch schematic (saved by Fritzing 0.9.3b)
breadboards: 1

parts:
  Part1 = Arduino Uno (Rev3)
  LED1 = RGB LED (com. cathode, rgb) [package="5 mm [THT]"]
  HC-SR04_Sensor_1 = HC-SR04 Ultrasonic Distance Sensor
  J1 = Piezo Speaker

nets:
  N1: Part1.D8, LED1.blue_anode
  N2: Part1.D9_PWM, LED1.green_anode
  N3: Part1.D5_PWM, J1.pin2
  N4: Part1.D6_PWM, HC-SR04_Sensor_1.ECHO
  N5: Part1.D7, HC-SR04_Sensor_1.TRIG
  5V: Part1.5V, LED1.red_anode, HC-SR04_Sensor_1.VCC
  GND: Part1.GND, HC-SR04_Sensor_1.GND, J1.pin1
